// Logisim project L0_CRC.circ as structural Verilog: 2 circuits, main circuit CRC
module CRC (
  input  [7:0] A,
  input  [3:0] B,
  output [10:0] out_3
);

  wire [2:0] div_1_c, div_2_c, div_3_c, div_4_c, div_5_c, div_6_c, div_7_c;

  div div_1 (.A(A[7:4]), .B(B), .C(div_1_c));  // open: D
  div div_2 (.A({div_1_c, A[3]}), .B(B), .C(div_2_c));  // open: D
  div div_3 (.A({div_2_c, A[2]}), .B(B), .C(div_3_c));  // open: D
  div div_4 (.A({div_3_c, A[1]}), .B(B), .C(div_4_c));  // open: D
  div div_5 (.A({div_4_c, A[0]}), .B(B), .C(div_5_c));  // open: D
  div div_6 (.A({div_5_c, 1'b0}), .B(B), .C(div_6_c));  // open: D
  div div_7 (.A({div_6_c, 1'b0}), .B(B), .C(div_7_c));  // open: D
  div div_8 (.A({div_7_c, 1'b0}), .B(B), .C(out_3[2:0]));  // open: D

  assign out_3[10:3] = A;
endmodule

module div (
  input  [3:0] A,
  input  [3:0] B,
  output [2:0] C,
  output D
);

  wire [3:0] xor_1_out;

  assign xor_1_out = A ^ B;  // XOR_Gate xor_1, 4 bits wide
  Multiplexer #(.select(1), .width(3), .disabled("Z"), .enable("false")) multiplexer_1 (
    .in0(A[2:0]), .in1(xor_1_out[2:0]), .out(C), .sel(A[3]));

  assign D = A[3];
endmodule
