// Logisim project L0_FSM.circ as structural Verilog: 1 circuit, main circuit fsm
module fsm (
  input  [1:0] in,
  input  clr,
  output out_3
);

  wire and_1_out, clock_1_out, counter_1_q, not_1_out, not_2_out, not_3_out;
  wire [5:0] multiplexer_1_out, register_1_q;
  wire [5:2] multiplexer_2_out;
  wire [5:4] multiplexer_2_out_2;

  Clock #(.highDuration(1), .lowDuration(1)) clock_1 (.out(clock_1_out));
  Multiplexer #(.select(1), .width(6), .disabled("Z"), .enable("false")) multiplexer_1 (
    .in0({multiplexer_2_out, in}), .in1({6{1'b1}}), .out(multiplexer_1_out), .sel(clr));
  Register #(.width(6), .trigger("rising"), .Select("low")) register_1 (
    .D(multiplexer_1_out), .Q(register_1_q), .clk(clock_1_out));  // open: en, clr
  Multiplexer #(.select(1), .width(6), .disabled("Z"), .enable("false")) multiplexer_2 (
    .in0({6{1'b1}}), .in1(register_1_q), .out({multiplexer_2_out_2, multiplexer_2_out}), .sel(counter_1_q));
  Counter #(.width(1), .max('h1), .ongoal("stay"), .trigger("rising"), .behavior("new")) counter_1 (
    .Q(counter_1_q), .clk(clock_1_out));  // open: load, D, count, carry, clr, preset, down
  not not_1 (not_1_out, in[0]);
  not not_2 (not_2_out, multiplexer_2_out[2]);
  not not_3 (not_3_out, multiplexer_2_out[5]);
  and and_1 (and_1_out, multiplexer_2_out[4], not_3_out);
  and and_2 (out_3, not_1_out, not_2_out, and_1_out);
endmodule
