// Logisim project L0_GRF.circ as structural Verilog: 1 circuit, main circuit grf
module grf (
  input  clk,
  input  WE,
  input  Reset,
  input  [31:0] WD,
  input  [4:0] A1,
  input  [4:0] A2,
  input  [4:0] A3,
  output [31:0] RD1,
  output [31:0] RD2
);

  wire [31:0] i1, i2, i3, i4, i5, i6, i7, i8, i9, i10, i11, i12, i13, i14, i15, i16, i17, i18, i19, i20, i21,
       i22, i23, i24, i25, i26, i27, i28, i29, i30, i31, o1, o2, o3, o4, o5, o6, o7, o8, o9, o10, o11, o12,
       o13, o14, o15, o16, o17, o18, o19, o20, o21, o22, o23, o24, o25, o26, o27, o28, o29, o30, o31;

  Register #(.width(32), .trigger("rising"), .Select("low")) register_1 (
    .D(i1), .en(WE), .Q(o1), .clk(clk), .clr(Reset));
  Register #(.width(32), .trigger("rising"), .Select("low")) register_2 (
    .D(i2), .en(WE), .Q(o2), .clk(clk), .clr(Reset));
  Register #(.width(32), .trigger("rising"), .Select("low")) register_3 (
    .D(i3), .en(WE), .Q(o3), .clk(clk), .clr(Reset));
  Register #(.width(32), .trigger("rising"), .Select("low")) register_4 (
    .D(i4), .en(WE), .Q(o4), .clk(clk), .clr(Reset));
  Register #(.width(32), .trigger("rising"), .Select("low")) register_5 (
    .D(i5), .en(WE), .Q(o5), .clk(clk), .clr(Reset));
  Register #(.width(32), .trigger("rising"), .Select("low")) register_6 (
    .D(i6), .en(WE), .Q(o6), .clk(clk), .clr(Reset));
  Register #(.width(32), .trigger("rising"), .Select("low")) register_7 (
    .D(i7), .en(WE), .Q(o7), .clk(clk), .clr(Reset));
  Multiplexer #(.select(5), .width(32), .disabled("Z"), .enable("false")) multiplexer_1 (
    .in0({32{1'b0}}), .in1(o1), .in2(o2), .in3(o3), .in4(o4), .in5(o5), .in6(o6), .in7(o7), .in8(o8),
    .in9(o9), .in10(o10), .in11(o11), .in12(o12), .in13(o13), .in14(o14), .in15(o15), .in16(o16), .in17(o17),
    .in18(o18), .in19(o19), .in20(o20), .in21(o21), .in22(o22), .in23(o23), .in24(o24), .in25(o25),
    .in26(o26), .in27(o27), .in28(o28), .in29(o29), .in30(o30), .in31(o31), .out(RD1), .sel(A1));
  Register #(.width(32), .trigger("rising"), .Select("low")) register_8 (
    .D(i8), .en(WE), .Q(o8), .clk(clk), .clr(Reset));
  Register #(.width(32), .trigger("rising"), .Select("low")) register_9 (
    .D(i9), .en(WE), .Q(o9), .clk(clk), .clr(Reset));
  Register #(.width(32), .trigger("rising"), .Select("low")) register_10 (
    .D(i10), .en(WE), .Q(o10), .clk(clk), .clr(Reset));
  Register #(.width(32), .trigger("rising"), .Select("low")) register_11 (
    .D(i11), .en(WE), .Q(o11), .clk(clk), .clr(Reset));
  Register #(.width(32), .trigger("rising"), .Select("low")) register_12 (
    .D(i12), .en(WE), .Q(o12), .clk(clk), .clr(Reset));
  Register #(.width(32), .trigger("rising"), .Select("low")) register_13 (
    .D(i13), .en(WE), .Q(o13), .clk(clk), .clr(Reset));
  Register #(.width(32), .trigger("rising"), .Select("low")) register_14 (
    .D(i14), .en(WE), .Q(o14), .clk(clk), .clr(Reset));
  Register #(.width(32), .trigger("rising"), .Select("low")) register_15 (
    .D(i15), .en(WE), .Q(o15), .clk(clk), .clr(Reset));
  Multiplexer #(.select(5), .width(32), .disabled("Z"), .enable("false")) multiplexer_2 (
    .in0({32{1'b0}}), .in1(o1), .in2(o2), .in3(o3), .in4(o4), .in5(o5), .in6(o6), .in7(o7), .in8(o8),
    .in9(o9), .in10(o10), .in11(o11), .in12(o12), .in13(o13), .in14(o14), .in15(o15), .in16(o16), .in17(o17),
    .in18(o18), .in19(o19), .in20(o20), .in21(o21), .in22(o22), .in23(o23), .in24(o24), .in25(o25),
    .in26(o26), .in27(o27), .in28(o28), .in29(o29), .in30(o30), .in31(o31), .out(RD2), .sel(A2));
  Register #(.width(32), .trigger("rising"), .Select("low")) register_16 (
    .D(i16), .en(WE), .Q(o16), .clk(clk), .clr(Reset));
  Register #(.width(32), .trigger("rising"), .Select("low")) register_17 (
    .D(i17), .en(WE), .Q(o17), .clk(clk), .clr(Reset));
  Register #(.width(32), .trigger("rising"), .Select("low")) register_18 (
    .D(i18), .en(WE), .Q(o18), .clk(clk), .clr(Reset));
  Register #(.width(32), .trigger("rising"), .Select("low")) register_19 (
    .D(i19), .en(WE), .Q(o19), .clk(clk), .clr(Reset));
  Register #(.width(32), .trigger("rising"), .Select("low")) register_20 (
    .D(i20), .en(WE), .Q(o20), .clk(clk), .clr(Reset));
  Register #(.width(32), .trigger("rising"), .Select("low")) register_21 (
    .D(i21), .en(WE), .Q(o21), .clk(clk), .clr(Reset));
  Register #(.width(32), .trigger("rising"), .Select("low")) register_22 (
    .D(i22), .en(WE), .Q(o22), .clk(clk), .clr(Reset));
  Register #(.width(32), .trigger("rising"), .Select("low")) register_23 (
    .D(i23), .en(WE), .Q(o23), .clk(clk), .clr(Reset));
  Demultiplexer #(.select(5), .width(32), .tristate("true"), .disabled("Z"), .enable("false")) demultiplexer_1 (
    .out1(i1), .out2(i2), .out3(i3), .out4(i4), .out5(i5), .out6(i6), .out7(i7), .out8(i8), .out9(i9),
    .out10(i10), .out11(i11), .out12(i12), .out13(i13), .out14(i14), .out15(i15), .out16(i16), .out17(i17),
    .out18(i18), .out19(i19), .out20(i20), .out21(i21), .out22(i22), .out23(i23), .out24(i24), .out25(i25),
    .out26(i26), .out27(i27), .out28(i28), .out29(i29), .out30(i30), .out31(i31), .in(WD), .sel(A3));  // open: out0
  Register #(.width(32), .trigger("rising"), .Select("low")) register_24 (
    .D(i24), .en(WE), .Q(o24), .clk(clk), .clr(Reset));
  Register #(.width(32), .trigger("rising"), .Select("low")) register_25 (
    .D(i25), .en(WE), .Q(o25), .clk(clk), .clr(Reset));
  Register #(.width(32), .trigger("rising"), .Select("low")) register_26 (
    .D(i26), .en(WE), .Q(o26), .clk(clk), .clr(Reset));
  Register #(.width(32), .trigger("rising"), .Select("low")) register_27 (
    .D(i27), .en(WE), .Q(o27), .clk(clk), .clr(Reset));
  Register #(.width(32), .trigger("rising"), .Select("low")) register_28 (
    .D(i28), .en(WE), .Q(o28), .clk(clk), .clr(Reset));
  Register #(.width(32), .trigger("rising"), .Select("low")) register_29 (
    .D(i29), .en(WE), .Q(o29), .clk(clk), .clr(Reset));
  Register #(.width(32), .trigger("rising"), .Select("low")) register_30 (
    .D(i30), .en(WE), .Q(o30), .clk(clk), .clr(Reset));
  Register #(.width(32), .trigger("rising"), .Select("low")) register_31 (
    .D(i31), .en(WE), .Q(o31), .clk(clk), .clr(Reset));

  // Other names for the same wires on the sheet: rst = Reset

  // Notes on the sheet:
  //   Reset: pull=down
endmodule
