// Logisim project L1_ftoi.circ as structural Verilog: 1 circuit, main circuit ftoi
module ftoi (
  input  [15:0] in_1,
  output [31:0] out_2
);

  wire comparator_1_lt;
  wire [4:0] subtractor_1_out;
  wire [16:0] multiplexer_1_out, negator_1_out;
  wire [25:0] bit_extender_1_out, shifter_1_out;
  wire [31:0] bit_extender_2_out;

  assign bit_extender_1_out = {{15{1'b0}}, {1'b1, in_1[9:0]}};  // Bit_Extender bit_extender_1
  Shifter #(.width(26), .shift("ll")) shifter_1 (
    .in(bit_extender_1_out), .\dist (subtractor_1_out), .out(shifter_1_out));
  Subtractor #(.width(5)) subtractor_1 (.a(in_1[14:10]), .b(5'b01111), .out(subtractor_1_out));  // open: bin, bout
  Comparator #(.width(5), .mode("twosComplement")) comparator_1 (
    .a(subtractor_1_out), .b({5{1'b0}}), .lt(comparator_1_lt));  // open: gt, eq
  Multiplexer #(.select(1), .width(17), .disabled("Z"), .enable("false")) multiplexer_1 (
    .in0({1'b0, shifter_1_out[25:10]}), .in1(negator_1_out), .out(multiplexer_1_out), .sel(in_1[15]));
  Negator #(.width(17)) negator_1 (.in({1'b0, shifter_1_out[25:10]}), .out(negator_1_out));
  assign bit_extender_2_out = {{15{multiplexer_1_out[16]}}, multiplexer_1_out};  // Bit_Extender bit_extender_2
  // Probe on out_2
  Multiplexer #(.select(1), .width(32), .disabled("Z"), .enable("false")) multiplexer_2 (
    .in0(bit_extender_2_out), .in1({32{1'b0}}), .out(out_2), .sel(comparator_1_lt));
endmodule
