// Logisim project L1_navigation.circ as structural Verilog: 2 circuits, main circuit navigation
module navigation (
  input  [1:0] dir,
  input  clk,
  input  reset,
  output arrive,
  output hit
);

  wire counter_1_q, hit_q, not_1_out, not_2_out, state_1_hit;
  wire [2:0] multiplexer_1_out, register_1_q, state_1_snext;

  Counter #(.width(1), .max('h1), .ongoal("stay"), .trigger("rising"), .behavior("new")) counter_1 (
    .Q(counter_1_q), .clk(clk));  // open: load, D, count, carry, clr, preset, down
  Register #(.width(3), .trigger("rising"), .Select("low")) register_1 (
    .D(state_1_snext), .Q(register_1_q), .clk(clk), .clr(reset));  // open: en
  Multiplexer #(.select(1), .width(3), .disabled("Z"), .enable("false")) multiplexer_1 (
    .in0(3'b000), .in1(register_1_q), .out(multiplexer_1_out), .sel(counter_1_q));
  state state_1 (.S0(multiplexer_1_out), .dir(dir), .Snext(state_1_snext), .hit(state_1_hit));
  Register #(.width(1), .trigger("rising"), .Select("low")) u_hit (
    .D(state_1_hit), .Q(hit_q), .clk(clk), .clr(reset));  // open: en
  Multiplexer #(.select(1), .width(1), .disabled("Z"), .enable("false")) multiplexer_2 (
    .in0(1'b0), .in1(hit_q), .out(hit), .sel(counter_1_q));
  and and_1 (arrive, register_1_q[2], not_1_out, not_2_out);
  not not_1 (not_1_out, register_1_q[1]);
  not not_2 (not_2_out, register_1_q[0]);
endmodule

module state (
  input  [2:0] S0,
  input  [1:0] dir,
  output [2:0] Snext,
  output hit
);

  wire and_1_out, and_2_out, and_3_out, and_4_out, and_5_out, and_6_out, and_7_out, and_8_out, and_9_out,
       and_10_out, and_11_out, and_12_out, and_13_out, and_14_out, and_15_out, and_16_out, or_1_out, out0,
       out1, out2, xnor_1_out, xor_1_out;
  wire [1:0] not_2_out;
  wire [2:0] multiplexer_1_out, not_1_out;

  assign not_1_out = ~S0;  // NOT_Gate not_1, 3 bits wide
  assign not_2_out = ~dir;  // NOT_Gate not_2, 2 bits wide
  or or_1 (or_1_out, dir[0], dir[1]);
  and and_1 (and_1_out, or_1_out, not_1_out[0], not_1_out[1], not_1_out[2]);
  and and_2 (and_2_out, dir[1], dir[0], S0[0], not_1_out[1], not_1_out[2]);
  xor xor_1 (xor_1_out, dir[1], dir[0]);
  and and_3 (and_3_out, xor_1_out, not_1_out[2], S0[1], not_1_out[0]);
  xnor xnor_1 (xnor_1_out, dir[1], dir[0]);
  and and_4 (and_4_out, xnor_1_out, not_1_out[2], S0[1], S0[0]);
  and and_5 (and_5_out, S0[2], not_1_out[1], not_1_out[0]);
  and and_6 (and_6_out, not_1_out[2], S0[1], not_1_out[0], not_2_out[1], not_2_out[0]);
  and and_7 (and_7_out, not_1_out[2], S0[1], S0[0], not_2_out[1], dir[0]);
  and and_8 (and_8_out, not_1_out[2], not_1_out[1], S0[0], not_2_out[1], not_2_out[0]);
  and and_9 (and_9_out, S0[2], not_1_out[1], not_1_out[0], dir[1], not_2_out[0]);
  and and_10 (and_10_out, S0[2], not_1_out[1], not_1_out[0], dir[1], dir[0]);
  and and_11 (and_11_out, not_1_out[2], not_1_out[1], not_1_out[0], not_2_out[1], not_2_out[0]);
  and and_12 (and_12_out, not_1_out[2], not_1_out[1], S0[0], not_2_out[1], not_2_out[0]);
  and and_13 (and_13_out, not_1_out[2], S0[1], not_1_out[0], dir[1], dir[0]);
  and and_14 (and_14_out, not_1_out[2], S0[1], S0[0], dir[1], not_2_out[0]);
  and and_15 (and_15_out, S0[2], not_1_out[1], not_1_out[0], dir[1], dir[0]);
  and and_16 (and_16_out, not_1_out[2], not_1_out[1], S0[0], not_2_out[1], dir[0]);
  or or_2 (out2, and_6_out, and_7_out);
  or or_3 (out0, and_11_out, and_12_out, and_13_out, and_14_out, and_15_out);
  Multiplexer #(.select(1), .width(3), .disabled("Z"), .enable("false")) multiplexer_1 (
    .in0({out2, out1, out0}), .in1(S0), .out(multiplexer_1_out), .sel(hit));
  or or_4 (hit, and_1_out, and_2_out, and_3_out, and_4_out);
  or or_5 (out1, and_8_out, and_9_out, and_10_out, and_16_out);
  Multiplexer #(.select(1), .width(3), .disabled("Z"), .enable("false")) multiplexer_2 (
    .in0(multiplexer_1_out), .in1(3'b000), .out(Snext), .sel(and_5_out));
endmodule
