// Logisim project CPU.circ as structural Verilog: 5 circuits, main circuit main
module main (
  input  rst,
  output [31:0] out_2,
  output out_3,
  output [4:0] out_4,
  output [31:0] out_5,
  output out_6,
  output [4:0] out_7,
  output [31:0] out_8
);

  wire alu_1_zero, ALUSrc, and_1_out, Brancheq, clk, MemToReg, RegDst;
  wire [2:0] ALUControl;
  wire [31:0] alu_1_c, bit_extender_1_out, grf_1_rd1, multiplexer_2_out, ram_1_data;

  Clock #(.highDuration(1), .lowDuration(1)) clock_1 (.out(clk));
  IFU ifu_1 (.clk(clk), .offset(bit_extender_1_out), .rst(rst), .Instr(out_2), .branch(and_1_out));
  Control control_1 (
    .op(out_2[31:26]), .func(out_2[5:0]), .RegDst(RegDst), .ALUSrc(ALUSrc), .MemToReg(MemToReg),
    .RegWrite(out_3), .MemWrite(out_6), .Brancheq(Brancheq), .ALUCtr(ALUControl));
  Multiplexer #(.select(1), .width(5), .disabled("Z"), .enable("false")) multiplexer_1 (
    .in0(out_2[20:16]), .in1(out_2[15:11]), .out(out_4), .sel(RegDst));
  GRF grf_1 (
    .A1(out_2[25:21]), .A2(out_2[20:16]), .A3(out_4), .RD1(grf_1_rd1), .RD2(out_8), .clk(clk), .WE(out_3),
    .Reset(rst), .WD(out_5));
  assign bit_extender_1_out = {{16{out_2[15]}}, out_2[15:0]};  // Bit_Extender bit_extender_1
  Multiplexer #(.select(1), .width(32), .disabled("Z"), .enable("false")) multiplexer_2 (
    .in0(out_8), .in1(bit_extender_1_out), .out(multiplexer_2_out), .sel(ALUSrc));
  ALU alu_1 (
    .A(grf_1_rd1), .B(multiplexer_2_out), .C({alu_1_c[31:7], out_7, alu_1_c[1:0]}), .ZERO(alu_1_zero),
    .F(ALUControl));
  and and_1 (and_1_out, alu_1_zero, Brancheq);
  RAM #(.addrWidth(5), .dataWidth(32), .bus("separate"), .Select("low")) ram_1 (
    .addr(out_7), .din(out_8), .data(ram_1_data), .str(out_6), .clk(clk), .clr(rst));  // open: sel, ld
  Multiplexer #(.select(1), .width(32), .disabled("Z"), .enable("false")) multiplexer_3 (
    .in0({alu_1_c[31:7], out_7, alu_1_c[1:0]}), .in1(ram_1_data), .out(out_5), .sel(MemToReg));

  // Other names for the same wires on the sheet: OMemA[4:0] = out_7; Instr[31:0] = out_2; MemWrite = out_6;
  //   OMemD[31:0] = out_8; ORegA[4:0] = out_4; RegWrite = out_3
endmodule

module GRF (
  input  clk,
  input  WE,
  input  Reset,
  input  [31:0] WD,
  input  [4:0] A1,
  input  [4:0] A2,
  input  [4:0] A3,
  output [31:0] RD1,
  output [31:0] RD2
);

  wire [31:0] i1, i2, i3, i4, i5, i6, i7, i8, i9, i10, i11, i12, i13, i14, i15, i16, i17, i18, i19, i20, i21,
       i22, i23, i24, i25, i26, i27, i28, i29, i30, i31, o1, o2, o3, o4, o5, o6, o7, o8, o9, o10, o11, o12,
       o13, o14, o15, o16, o17, o18, o19, o20, o21, o22, o23, o24, o25, o26, o27, o28, o29, o30, o31;

  Register #(.width(32), .trigger("rising"), .Select("low")) register_1 (
    .D(i1), .en(WE), .Q(o1), .clk(clk), .clr(Reset));
  Register #(.width(32), .trigger("rising"), .Select("low")) register_2 (
    .D(i2), .en(WE), .Q(o2), .clk(clk), .clr(Reset));
  Register #(.width(32), .trigger("rising"), .Select("low")) register_3 (
    .D(i3), .en(WE), .Q(o3), .clk(clk), .clr(Reset));
  Register #(.width(32), .trigger("rising"), .Select("low")) register_4 (
    .D(i4), .en(WE), .Q(o4), .clk(clk), .clr(Reset));
  Register #(.width(32), .trigger("rising"), .Select("low")) register_5 (
    .D(i5), .en(WE), .Q(o5), .clk(clk), .clr(Reset));
  Register #(.width(32), .trigger("rising"), .Select("low")) register_6 (
    .D(i6), .en(WE), .Q(o6), .clk(clk), .clr(Reset));
  Register #(.width(32), .trigger("rising"), .Select("low")) register_7 (
    .D(i7), .en(WE), .Q(o7), .clk(clk), .clr(Reset));
  Multiplexer #(.select(5), .width(32), .disabled("Z"), .enable("false")) multiplexer_1 (
    .in0({32{1'b0}}), .in1(o1), .in2(o2), .in3(o3), .in4(o4), .in5(o5), .in6(o6), .in7(o7), .in8(o8),
    .in9(o9), .in10(o10), .in11(o11), .in12(o12), .in13(o13), .in14(o14), .in15(o15), .in16(o16), .in17(o17),
    .in18(o18), .in19(o19), .in20(o20), .in21(o21), .in22(o22), .in23(o23), .in24(o24), .in25(o25),
    .in26(o26), .in27(o27), .in28(o28), .in29(o29), .in30(o30), .in31(o31), .out(RD1), .sel(A1));
  Register #(.width(32), .trigger("rising"), .Select("low")) register_8 (
    .D(i8), .en(WE), .Q(o8), .clk(clk), .clr(Reset));
  Register #(.width(32), .trigger("rising"), .Select("low")) register_9 (
    .D(i9), .en(WE), .Q(o9), .clk(clk), .clr(Reset));
  Register #(.width(32), .trigger("rising"), .Select("low")) register_10 (
    .D(i10), .en(WE), .Q(o10), .clk(clk), .clr(Reset));
  Register #(.width(32), .trigger("rising"), .Select("low")) register_11 (
    .D(i11), .en(WE), .Q(o11), .clk(clk), .clr(Reset));
  Register #(.width(32), .trigger("rising"), .Select("low")) register_12 (
    .D(i12), .en(WE), .Q(o12), .clk(clk), .clr(Reset));
  Register #(.width(32), .trigger("rising"), .Select("low")) register_13 (
    .D(i13), .en(WE), .Q(o13), .clk(clk), .clr(Reset));
  Register #(.width(32), .trigger("rising"), .Select("low")) register_14 (
    .D(i14), .en(WE), .Q(o14), .clk(clk), .clr(Reset));
  Register #(.width(32), .trigger("rising"), .Select("low")) register_15 (
    .D(i15), .en(WE), .Q(o15), .clk(clk), .clr(Reset));
  Multiplexer #(.select(5), .width(32), .disabled("Z"), .enable("false")) multiplexer_2 (
    .in0({32{1'b0}}), .in1(o1), .in2(o2), .in3(o3), .in4(o4), .in5(o5), .in6(o6), .in7(o7), .in8(o8),
    .in9(o9), .in10(o10), .in11(o11), .in12(o12), .in13(o13), .in14(o14), .in15(o15), .in16(o16), .in17(o17),
    .in18(o18), .in19(o19), .in20(o20), .in21(o21), .in22(o22), .in23(o23), .in24(o24), .in25(o25),
    .in26(o26), .in27(o27), .in28(o28), .in29(o29), .in30(o30), .in31(o31), .out(RD2), .sel(A2));
  Register #(.width(32), .trigger("rising"), .Select("low")) register_16 (
    .D(i16), .en(WE), .Q(o16), .clk(clk), .clr(Reset));
  Register #(.width(32), .trigger("rising"), .Select("low")) register_17 (
    .D(i17), .en(WE), .Q(o17), .clk(clk), .clr(Reset));
  Register #(.width(32), .trigger("rising"), .Select("low")) register_18 (
    .D(i18), .en(WE), .Q(o18), .clk(clk), .clr(Reset));
  Register #(.width(32), .trigger("rising"), .Select("low")) register_19 (
    .D(i19), .en(WE), .Q(o19), .clk(clk), .clr(Reset));
  Register #(.width(32), .trigger("rising"), .Select("low")) register_20 (
    .D(i20), .en(WE), .Q(o20), .clk(clk), .clr(Reset));
  Register #(.width(32), .trigger("rising"), .Select("low")) register_21 (
    .D(i21), .en(WE), .Q(o21), .clk(clk), .clr(Reset));
  Register #(.width(32), .trigger("rising"), .Select("low")) register_22 (
    .D(i22), .en(WE), .Q(o22), .clk(clk), .clr(Reset));
  Register #(.width(32), .trigger("rising"), .Select("low")) register_23 (
    .D(i23), .en(WE), .Q(o23), .clk(clk), .clr(Reset));
  Demultiplexer #(.select(5), .width(32), .tristate("true"), .disabled("Z"), .enable("false")) demultiplexer_1 (
    .out1(i1), .out2(i2), .out3(i3), .out4(i4), .out5(i5), .out6(i6), .out7(i7), .out8(i8), .out9(i9),
    .out10(i10), .out11(i11), .out12(i12), .out13(i13), .out14(i14), .out15(i15), .out16(i16), .out17(i17),
    .out18(i18), .out19(i19), .out20(i20), .out21(i21), .out22(i22), .out23(i23), .out24(i24), .out25(i25),
    .out26(i26), .out27(i27), .out28(i28), .out29(i29), .out30(i30), .out31(i31), .in(WD), .sel(A3));  // open: out0
  Register #(.width(32), .trigger("rising"), .Select("low")) register_24 (
    .D(i24), .en(WE), .Q(o24), .clk(clk), .clr(Reset));
  Register #(.width(32), .trigger("rising"), .Select("low")) register_25 (
    .D(i25), .en(WE), .Q(o25), .clk(clk), .clr(Reset));
  Register #(.width(32), .trigger("rising"), .Select("low")) register_26 (
    .D(i26), .en(WE), .Q(o26), .clk(clk), .clr(Reset));
  Register #(.width(32), .trigger("rising"), .Select("low")) register_27 (
    .D(i27), .en(WE), .Q(o27), .clk(clk), .clr(Reset));
  Register #(.width(32), .trigger("rising"), .Select("low")) register_28 (
    .D(i28), .en(WE), .Q(o28), .clk(clk), .clr(Reset));
  Register #(.width(32), .trigger("rising"), .Select("low")) register_29 (
    .D(i29), .en(WE), .Q(o29), .clk(clk), .clr(Reset));
  Register #(.width(32), .trigger("rising"), .Select("low")) register_30 (
    .D(i30), .en(WE), .Q(o30), .clk(clk), .clr(Reset));
  Register #(.width(32), .trigger("rising"), .Select("low")) register_31 (
    .D(i31), .en(WE), .Q(o31), .clk(clk), .clr(Reset));

  // Other names for the same wires on the sheet: rst = Reset

  // Notes on the sheet:
  //   Reset: pull=down
endmodule

module ALU (
  input  [31:0] A,
  input  [31:0] B,
  input  [2:0] F,
  output [31:0] C,
  output ZERO
);

  wire [31:0] addu, ori, subu;

  Adder #(.width(32)) adder_1 (.a(A), .b(B), .out(addu));  // open: cin, cout
  Subtractor #(.width(32)) subtractor_1 (.a(A), .b(B), .out(subu));  // open: bin, bout
  assign ori = A | {{16{1'b0}}, B[15:0]};  // OR_Gate or_1, 32 bits wide
  Comparator #(.width(32), .mode("unsigned")) comparator_1 (.a(A), .b(B), .eq(ZERO));  // open: gt, lt
  Multiplexer #(.select(3), .width(32), .disabled("Z"), .enable("false")) multiplexer_1 (
    .in0(addu), .in1(subu), .in2(ori), .in3({B[15:0], {16{1'b0}}}), .out(C), .sel(F));  // open: in4, in5, in6, in7

  // Other names for the same wires on the sheet: lui[31:16] = B[15:0]
endmodule

module Control (
  input  [5:0] op,
  input  [5:0] func,
  output RegDst,
  output ALUSrc,
  output MemToReg,
  output RegWrite,
  output MemWrite,
  output Brancheq,
  output [2:0] ALUCtr
);

  wire addu_out, cal_out, lui_out, lw_out, ori_out, subu_out, sw_out;
  wire [5:0] not_1_out, not_2_out;

  assign not_1_out = ~func;  // NOT_Gate not_1, 6 bits wide
  assign not_2_out = ~op;  // NOT_Gate not_2, 6 bits wide
  and cal (cal_out, not_2_out[5], not_2_out[4], not_2_out[3], not_2_out[2], not_2_out[1], not_2_out[0]);
  and addu (addu_out, cal_out, func[5], not_1_out[4], not_1_out[3], not_1_out[2], not_1_out[1], 1'b1);
  and subu (subu_out, cal_out, func[5], not_1_out[4], not_1_out[3], not_1_out[2], func[1], 1'b1);
  and lui (lui_out, not_2_out[5], not_2_out[4], op[3], op[2], op[1], op[0]);
  and ori (ori_out, not_2_out[5], not_2_out[4], op[3], op[2], not_2_out[1], op[0]);
  and sw (sw_out, op[5], not_2_out[4], op[3], not_2_out[2], op[1], op[0]);
  and lw (lw_out, op[5], not_2_out[4], not_2_out[3], not_2_out[2], op[1], op[0]);
  and beq (Brancheq, not_2_out[5], not_2_out[4], not_2_out[3], op[2], not_2_out[1], not_2_out[0]);
  // AND_Gate nop has open pins: in0=not_2_out[5], in1=not_2_out[4], in2=not_2_out[3], in3=not_2_out[2], in4=not_2_out[1], in5=not_2_out[0], out=open
  or or_1 (RegDst, addu_out, subu_out);
  or or_2 (ALUSrc, lui_out, ori_out, sw_out, lw_out);
  buf or_3 (MemToReg, lw_out);  // OR_Gate
  or or_4 (RegWrite, addu_out, subu_out, lui_out, ori_out, lw_out);
  buf or_5 (MemWrite, sw_out);  // OR_Gate
  or ALUCtr1 (ALUCtr[1], lui_out, ori_out);
  or ALUCtr0 (ALUCtr[0], subu_out, lui_out);

  assign ALUCtr[2] = 1'b0;
endmodule

module IFU (
  input  branch,
  input  clk,
  input  [31:0] offset,
  input  rst,
  output [31:0] Instr
);

  wire [31:0] adder_1_out, adder_2_out, multiplexer_1_out, PC_q, shifter_1_out;

  Multiplexer #(.select(1), .width(32), .disabled("Z"), .enable("false")) multiplexer_1 (
    .in0(adder_1_out), .in1(adder_2_out), .out(multiplexer_1_out), .sel(branch));
  Register #(.width(32), .trigger("rising"), .Select("low")) PC (
    .D(multiplexer_1_out), .Q(PC_q), .clk(clk), .clr(rst));  // open: en
  Adder #(.width(32)) adder_1 (.a(PC_q), .b(32'h4), .out(adder_1_out));  // open: cin, cout
  ROM #(.addrWidth(5), .dataWidth(32), .Select("low")) rom_1 (.addr(PC_q[6:2]), .data(Instr));
  Shifter #(.width(32), .shift("ll")) shifter_1 (.in(offset), .\dist (5'b00010), .out(shifter_1_out));
  Adder #(.width(32)) adder_2 (.a(shifter_1_out), .b(adder_1_out), .out(adder_2_out));  // open: cin, cout

  // Notes on the sheet:
  //   contents of rom_1 (hex, n*v repeats v):
  //   341c0000 341d0000 34013456 210820 8c010004 ac010004 3c027878 411822 3c051234 34040005 0 ac85ffff
  //   8c83ffff 10650001 1000000d 34670404 10e3000b 0 3c087777 3508ffff 80022 34001100 e65020 34080000
  //   34090001 340a0001 10a4020 1109fffe 1000ffff
endmodule
