// Logisim project fibo.circ as structural Verilog: 1 circuit, main circuit main
module main (
  input  [2:0] in_1,
  output [3:0] out_2
);

  wire and_1_out, and_2_out, clock_1_out, comparator_1_eq, comparator_2_eq, comparator_2_gt, comparator_3_lt,
       not_1_out, or_1_out;
  wire [3:0] adder_1_out, bit_extender_2_out, multiplexer_1_out, multiplexer_2_out, register_1_q,
       register_2_q;
  wire [6:0] bit_extender_1_out, counter_1_q;

  and and_1 (and_1_out, clock_1_out, not_1_out);
  Clock #(.highDuration(1), .lowDuration(1)) clock_1 (.out(clock_1_out));
  Register #(.width(4), .trigger("rising"), .Select("low")) register_1 (
    .D(adder_1_out), .Q(register_1_q), .clk(and_1_out));  // open: en, clr
  Register #(.width(4), .trigger("rising"), .Select("low")) register_2 (
    .D(register_1_q), .Q(register_2_q), .clk(and_2_out));  // open: en, clr
  and and_2 (and_2_out, clock_1_out, not_1_out);
  Counter #(.width(7), .max('h7f), .ongoal("wrap"), .trigger("rising"), .behavior("new")) counter_1 (
    .Q(counter_1_q), .clk(clock_1_out));  // open: load, D, count, carry, clr, preset, down
  assign bit_extender_1_out = {{4{1'b0}}, in_1};  // Bit_Extender bit_extender_1
  Adder #(.width(4)) adder_1 (.a(multiplexer_1_out), .b(register_2_q), .out(adder_1_out));  // open: cin, cout
  Comparator #(.width(4), .mode("unsigned")) comparator_1 (
    .a(register_1_q), .b(4'b0000), .eq(comparator_1_eq));  // open: gt, lt
  not not_1 (not_1_out, or_1_out);
  Comparator #(.width(7), .mode("unsigned")) comparator_2 (
    .a(counter_1_q), .b(bit_extender_1_out), .gt(comparator_2_gt), .eq(comparator_2_eq));  // open: lt
  Comparator #(.width(3), .mode("unsigned")) comparator_3 (.a(in_1), .b(3'b010), .lt(comparator_3_lt));  // open: gt, eq
  Multiplexer #(.select(1), .width(4), .disabled("Z"), .enable("false")) multiplexer_1 (
    .in0(register_1_q), .in1(4'b0001), .out(multiplexer_1_out), .sel(comparator_1_eq));
  or or_1 (or_1_out, comparator_2_gt, comparator_2_eq);
  Multiplexer #(.select(1), .width(4), .disabled("Z"), .enable("false")) multiplexer_2 (
    .in0(multiplexer_1_out), .in1(bit_extender_2_out), .out(multiplexer_2_out), .sel(comparator_3_lt));
  assign bit_extender_2_out = {{1{1'b0}}, in_1};  // Bit_Extender bit_extender_2
  Multiplexer #(.select(1), .width(4), .disabled("Z"), .enable("false")) multiplexer_3 (
    .in0(4'b0000), .in1(multiplexer_2_out), .out(out_2), .sel(or_1_out));
endmodule
