// Logisim project mod.circ as structural Verilog: 1 circuit, main circuit mod5
module mod5 (
  input  In,
  output S0,
  output S1,
  output S2,
  output S3,
  output S4
);

  wire and_1_out, and_2_out, and_3_out, and_4_out, and_5_out, and_6_out, and_7_out, and_8_out, clock_1_out,
       nor_1_out, nor_2_out, not_1_out;
  wire [3:0] register_1_q;

  Clock #(.highDuration(1), .lowDuration(1)) clock_1 (.out(clock_1_out));
  nor nor_1 (nor_1_out, register_1_q[3], register_1_q[2], In, register_1_q[1], register_1_q[0]);
  nor nor_2 (nor_2_out, register_1_q[3], register_1_q[2], not_1_out, register_1_q[1], register_1_q[0]);
  not not_1 (not_1_out, In);
  and and_1 (and_1_out, register_1_q[0], not_1_out);
  and and_2 (and_2_out, register_1_q[3], not_1_out);
  and and_3 (and_3_out, register_1_q[0], In);
  and and_4 (and_4_out, register_1_q[3], In);
  and and_5 (and_5_out, register_1_q[1], In);
  and and_6 (and_6_out, register_1_q[2], In);
  and and_7 (and_7_out, register_1_q[1], not_1_out);
  and and_8 (and_8_out, register_1_q[2], not_1_out);
  Register #(.width(4), .trigger("rising"), .Select("low")) register_1 (
    .D({S4, S3, S2, S1}), .Q(register_1_q), .clk(clock_1_out));  // open: en, clr
  or or_1 (S1, and_1_out, nor_1_out, and_2_out);
  or or_2 (S2, and_3_out, nor_2_out, and_4_out);
  or or_3 (S3, and_5_out, and_6_out);
  or or_4 (S4, and_7_out, and_8_out);

  assign S0 = 1'b0;
endmodule
