// Logisim project fibo+.circ as structural Verilog: 4 circuits, main circuit calc
module matrix (
  input  [31:0] a11,
  input  [31:0] a12,
  input  clk,
  input  [31:0] a21,
  input  [31:0] a22,
  output [31:0] a11_2,
  output [31:0] a12_2,
  output [31:0] a22_2,
  output [31:0] a21_2
);

  wire counter_1_q;
  wire [31:0] register_1_q, register_2_q, register_3_q;

  Counter #(.width(1), .max('h1), .ongoal("stay"), .trigger("rising"), .behavior("new")) counter_1 (
    .Q(counter_1_q), .clk(clk));  // open: load, D, count, carry, clr, preset, down
  Register #(.width(32), .trigger("rising"), .Select("low")) register_1 (
    .D(a11), .Q(register_1_q), .clk(clk));  // open: en, clr
  Register #(.width(32), .trigger("rising"), .Select("low")) register_2 (
    .D(a21), .Q(register_2_q), .clk(clk));  // open: en, clr
  Multiplexer #(.select(1), .width(32), .disabled("Z"), .enable("false")) multiplexer_1 (
    .in0(32'h1), .in1(register_1_q), .out(a11_2), .sel(counter_1_q));
  Multiplexer #(.select(1), .width(32), .disabled("Z"), .enable("false")) multiplexer_2 (
    .in0(32'h1), .in1(register_2_q), .out(a21_2), .sel(counter_1_q));
  Register #(.width(32), .trigger("rising"), .Select("low")) register_3 (
    .D(a12), .Q(register_3_q), .clk(clk));  // open: en, clr
  Register #(.width(32), .trigger("rising"), .Select("low")) register_4 (
    .D(a22), .Q(a22_2), .clk(clk));  // open: en, clr
  Multiplexer #(.select(1), .width(32), .disabled("Z"), .enable("false")) multiplexer_3 (
    .in0(32'h1), .in1(register_3_q), .out(a12_2), .sel(counter_1_q));
endmodule

module calc (
  input  clk,
  input  [31:0] init,
  output [31:0] ans,
  output done
);

  wire and_1_out, counter_1_q;
  wire [31:0] exp_a11_2, exp_a12_2, exp_a21_2, exp_a22_2, multiplexer_1_out, multiply_1_out_9,
       multiply_1_out_10, multiply_1_out_11, multiply_1_out_12, multiply_2_out_9, multiply_2_out_10,
       multiply_2_out_11, multiply_2_out_12, out_a12_2, out_a21_2, out_a22_2, register_1_q, shifter_1_out;

  matrix exp (
    .a11(multiply_1_out_9), .a12(multiply_1_out_10), .clk(clk), .a21(multiply_1_out_11),
    .a22(multiply_1_out_12), .a11_2(exp_a11_2), .a12_2(exp_a12_2), .a21_2(exp_a21_2), .a22_2(exp_a22_2));
  matrix out (
    .a11(multiply_2_out_9), .a12(multiply_2_out_10), .clk(and_1_out), .a21(multiply_2_out_11),
    .a22(multiply_2_out_12), .a11_2(ans), .a12_2(out_a12_2), .a21_2(out_a21_2), .a22_2(out_a22_2));
  and and_1 (and_1_out, clk, multiplexer_1_out[0]);
  multiply multiply_1 (
    .in_1(exp_a11_2), .in_3(exp_a12_2), .in_5(exp_a21_2), .in_7(exp_a22_2), .in_2(exp_a11_2),
    .in_4(exp_a12_2), .in_6(exp_a21_2), .in_8(exp_a22_2), .out_9(multiply_1_out_9),
    .out_10(multiply_1_out_10), .out_11(multiply_1_out_11), .out_12(multiply_1_out_12));
  multiply multiply_2 (
    .in_1(ans), .in_3(out_a12_2), .in_5(out_a21_2), .in_7(out_a22_2), .in_2(exp_a11_2), .in_4(exp_a12_2),
    .in_6(exp_a21_2), .in_8(exp_a22_2), .out_9(multiply_2_out_9), .out_10(multiply_2_out_10),
    .out_11(multiply_2_out_11), .out_12(multiply_2_out_12));
  Comparator #(.width(32), .mode("unsigned")) comparator_1 (
    .a(multiplexer_1_out), .b({32{1'b0}}), .eq(done));  // open: gt, lt
  Counter #(.width(1), .max('h1), .ongoal("stay"), .trigger("falling"), .behavior("new")) counter_1 (
    .Q(counter_1_q), .clk(clk));  // open: load, D, count, carry, clr, preset, down
  Register #(.width(32), .trigger("falling"), .Select("low")) register_1 (
    .D(shifter_1_out), .Q(register_1_q), .clk(clk));  // open: en, clr
  Multiplexer #(.select(1), .width(32), .disabled("Z"), .enable("false")) multiplexer_1 (
    .in0(init), .in1(register_1_q), .out(multiplexer_1_out), .sel(counter_1_q));
  Shifter #(.width(32), .shift("lr")) shifter_1 (.in(multiplexer_1_out), .\dist (5'b00001), .out(shifter_1_out));
endmodule

module multiply (
  input  [31:0] in_1,
  input  [31:0] in_2,
  input  [31:0] in_3,
  input  [31:0] in_4,
  input  [31:0] in_5,
  input  [31:0] in_6,
  input  [31:0] in_7,
  input  [31:0] in_8,
  output [31:0] out_9,
  output [31:0] out_10,
  output [31:0] out_11,
  output [31:0] out_12
);

  wire [31:0] multiplier_1_out, multiplier_2_out, multiplier_3_out, multiplier_4_out, multiplier_5_out,
       multiplier_6_out, multiplier_7_out, multiplier_8_out;

  Multiplier #(.width(32)) multiplier_1 (.a(in_1), .b(in_2), .out(multiplier_1_out));  // open: cin, cout
  Multiplier #(.width(32)) multiplier_2 (.a(in_3), .b(in_6), .out(multiplier_2_out));  // open: cin, cout
  Multiplier #(.width(32)) multiplier_3 (.a(in_1), .b(in_4), .out(multiplier_3_out));  // open: cin, cout
  Multiplier #(.width(32)) multiplier_4 (.a(in_3), .b(in_8), .out(multiplier_4_out));  // open: cin, cout
  Multiplier #(.width(32)) multiplier_5 (.a(in_5), .b(in_2), .out(multiplier_5_out));  // open: cin, cout
  Multiplier #(.width(32)) multiplier_6 (.a(in_7), .b(in_6), .out(multiplier_6_out));  // open: cin, cout
  Multiplier #(.width(32)) multiplier_7 (.a(in_5), .b(in_4), .out(multiplier_7_out));  // open: cin, cout
  Multiplier #(.width(32)) multiplier_8 (.a(in_7), .b(in_8), .out(multiplier_8_out));  // open: cin, cout
  Adder #(.width(32)) adder_1 (.a(multiplier_1_out), .b(multiplier_2_out), .out(out_9));  // open: cin, cout
  Adder #(.width(32)) adder_2 (.a(multiplier_3_out), .b(multiplier_4_out), .out(out_10));  // open: cin, cout
  Adder #(.width(32)) adder_3 (.a(multiplier_5_out), .b(multiplier_6_out), .out(out_11));  // open: cin, cout
  Adder #(.width(32)) adder_4 (.a(multiplier_7_out), .b(multiplier_8_out), .out(out_12));  // open: cin, cout

  // Other names for the same wires on the sheet: a11[31:0] = in_1; a12[31:0] = in_3; a21[31:0] = in_5;
  //   a22[31:0] = in_7; b11[31:0] = in_2; b12[31:0] = in_4; b21[31:0] = in_6; b22[31:0] = in_8; c11[31:0] = out_9;
  //   c12[31:0] = out_10; c21[31:0] = out_11; c22[31:0] = out_12
endmodule

module main (
  input  [31:0] in_1,
  output [31:0] out_2
);

  wire calc_1_done, clock_1_out, comparator_1_lt;
  wire [31:0] calc_1_ans, multiplexer_1_out, subtractor_1_out;

  Subtractor #(.width(32)) subtractor_1 (.a(in_1), .b(32'h2), .out(subtractor_1_out));  // open: bin, bout
  calc calc_1 (.init(subtractor_1_out), .ans(calc_1_ans), .done(calc_1_done), .clk(clock_1_out));
  Clock #(.highDuration(1), .lowDuration(1)) clock_1 (.out(clock_1_out));
  Multiplexer #(.select(1), .width(32), .disabled("Z"), .enable("false")) multiplexer_1 (
    .in0({32{1'b0}}), .in1(calc_1_ans), .out(multiplexer_1_out), .sel(calc_1_done));
  Comparator #(.width(32), .mode("unsigned")) comparator_1 (.a(in_1), .b(32'h2), .lt(comparator_1_lt));  // open: gt, eq
  Multiplexer #(.select(1), .width(32), .disabled("Z"), .enable("false")) multiplexer_2 (
    .in0(multiplexer_1_out), .in1(in_1), .out(out_2), .sel(comparator_1_lt));
endmodule
